// Logisim project proj_2_1.circ as structural Verilog: 6 circuits, main circuit testbench
module inst_fetch (
  input  clk,
  input  rst,
  input  control_en_i,
  input  [31:0] control_pc_i,
  input  [15:0] inst_i,
  output inst_en_o,
  output [31:0] current_pc_o,
  output [31:0] inst_addr_o,
  output [15:0] inst_o
);

  wire not_1_out, not_2_out;
  wire [31:0] adder_1_out, counter_1_q, multiplexer_1_out;

  not not_1 (not_1_out, rst);
  Adder #(.width(32)) adder_1 (.a(control_pc_i), .b(32'h1), .out(adder_1_out));  // open: cin, cout
  Counter #(.max('hffffffff), .width(32)) counter_1 (
    .clr(rst), .load(control_en_i), .up(not_1_out), .count(not_1_out), .clk(clk), .D(adder_1_out),
    .Q(counter_1_q));  // open: carry
  Multiplexer #(.width(32)) multiplexer_1 (
    .in0(counter_1_q), .in1(control_pc_i), .out(multiplexer_1_out), .sel(control_en_i));
  not not_2 (not_2_out, rst);
  Register #(.width(32)) register_1 (.D(multiplexer_1_out), .en(not_2_out), .clk(clk), .Q(current_pc_o), .clr(rst));
  not not_3 (inst_en_o, rst);

  assign inst_addr_o = current_pc_o;
  assign inst_o = inst_i;

  // Notes on the sheet:
  //   Don't touch
endmodule

module TOP (
  input  rst,
  input  clk,
  input  [15:0] inst,
  input  [31:0] mem_result,
  input  [31:0] current_pc,
  output mem_wen,
  output [31:0] mem_din,
  output mem_ren,
  output [31:0] alu_result,
  output control_en,
  output [31:0] control_pc,
  output wb_en,
  output [4:0] wb_addr,
  output [31:0] wb_data
);

  wire [31:0] imm_I, multiplexer_1_out, regfile_1_rd_value_o, regfile_1_rs2_value_o, rs1_short;

  assign imm_I = {{26{inst[12]}}, {inst[12], inst[6:2]}};  // Bit_Extender bit_extender_1
  PC pc_1 (
    .instr(inst), .current_pc(current_pc), .FUNC4(inst[12]), .select_type({inst[1:0], inst[15:13]}),
    .clk(clk), .rst(rst), .rs1(regfile_1_rd_value_o), .rs1_short_value(rs1_short), .control_pc(control_pc),
    .wb_en(wb_en), .control_en(control_en));
  Regfile regfile_1 (
    .in_1(clk), .inst(inst), .rd_value(alu_result), .rd_value_o(regfile_1_rd_value_o),
    .rs2_value_o(regfile_1_rs2_value_o), .rd_o(wb_addr), .rs1_short_value_o(rs1_short));
  Multiplexer #(.select(5), .width(32)) multiplexer_1 (
    .in8(imm_I), .in10(imm_I), .in11(imm_I), .in16(imm_I), .in20(regfile_1_rs2_value_o),
    .out(multiplexer_1_out), .sel({inst[1:0], inst[15:13]}));  // open: in0, in1, in2, in3, in4, in5, in6, in7, in9, in12, in13, in14, in15, in17, in18, in19, in21, in22, in23, in24, in25, in26, in27, in28, in29, in30, in31
  ALU alu_1 (
    .FUNC4(inst[12]), .rd_input(regfile_1_rd_value_o), .rs2_imm_input(multiplexer_1_out),
    .select_type({inst[1:0], inst[15:13]}), .clk(clk), .rst(rst), .rd_value_o(alu_result));

  assign mem_din = {32{1'b0}};
  assign mem_ren = 1'b0;
  assign mem_wen = 1'b0;
  assign wb_data = alu_result;

  // Other names for the same wires on the sheet: FUNC4 = inst[12]; FUNC3[2:0] = inst[15:13];
  //   select_type[4:0] = {inst[1:0], inst[15:13]}; OP[1:0] = inst[1:0]

  // Notes on the sheet:
  //   Fixed I/O
  //   Don't touch
endmodule

module testbench (
  input  rst,
  output mem_wen,
  output [31:0] mem_din,
  output mem_ren,
  output [31:0] alu_result,
  output control_en,
  output [31:0] control_pc,
  output halt,
  output wb_en,
  output [4:0] wb_addr,
  output [31:0] wb_data
);

  wire clk, inst_en, not_1_out, not_2_out, not_3_out, not_4_out, por_1_out, rst_t;
  wire [15:0] inst, inst_i;
  wire [31:0] current_pc, inst_addr, mem_result;

  not not_1 (not_1_out, inst_i[0]);
  not not_2 (not_2_out, inst_i[1]);
  not not_3 (not_3_out, inst_i[13]);
  not not_4 (not_4_out, inst_i[14]);
  and and_1 (halt, not_1_out, not_2_out, not_3_out, not_4_out, inst_i[15]);
  Clock clock_1 (.out(clk));
  or or_1 (rst_t, rst, por_1_out);
  POR por_1 (.out(por_1_out));
  inst_fetch inst_fetch_1 (
    .clk(clk), .rst(rst_t), .control_en_i(control_en), .control_pc_i(control_pc), .inst_i(inst_i),
    .inst_en_o(inst_en), .current_pc_o(current_pc), .inst_addr_o(inst_addr), .inst_o(inst));
  TOP top_1 (
    .rst(rst_t), .clk(clk), .inst(inst), .mem_result(mem_result), .current_pc(current_pc), .mem_wen(mem_wen),
    .mem_din(mem_din), .mem_ren(mem_ren), .alu_result(alu_result), .control_en(control_en),
    .control_pc(control_pc), .wb_en(wb_en), .wb_addr(wb_addr), .wb_data(wb_data));
  ROM #(.dataWidth(16)) rom_1 (.addr(inst_addr[7:0]), .data(inst_i));
  RAM #(.addrWidth(16), .clearpin("true"), .dataWidth(32), .\type ("nonvolatile")) ram_1 (
    .addr(alu_result[15:0]), .we(mem_wen), .oe(mem_ren), .clk(clk), .din(mem_din), .dout(mem_result),
    .clr(rst_t));

  // Notes on the sheet:
  //   contents of rom_1 (hex, n*v repeats v):
  //   4425 6525 40e 942a 84a2 49d 8000 1 1
  //   you can write any instruction in
endmodule

module Regfile (
  input  in_1,
  input  [15:0] inst,
  input  [31:0] rd_value,
  output [31:0] rd_value_o,
  output [31:0] rs2_value_o,
  output [4:0] rd_o,
  output [31:0] rs1_short_value_o
);

  wire decoder_1_out0, decoder_1_out2, decoder_1_out8, decoder_1_out9, decoder_1_out10, decoder_1_out11,
       decoder_1_out12, decoder_1_out13, decoder_1_out14, decoder_1_out15;
  wire [31:0] register_1_q, register_2_q, register_3_q, register_4_q, register_5_q, register_6_q,
       register_7_q, register_8_q, register_9_q, register_10_q;

  Decoder #(.select(5)) decoder_1 (
    .out0(decoder_1_out0), .out2(decoder_1_out2), .out8(decoder_1_out8), .out9(decoder_1_out9),
    .out10(decoder_1_out10), .out11(decoder_1_out11), .out12(decoder_1_out12), .out13(decoder_1_out13),
    .out14(decoder_1_out14), .out15(decoder_1_out15), .sel(inst[11:7]));  // open: out1, out3, out4, out5, out6, out7, out16, out17, out18, out19, out20, out21, out22, out23, out24, out25, out26, out27, out28, out29, out30, out31, en
  Register #(.width(32)) register_1 (.D(rd_value), .en(decoder_1_out0), .clk(in_1), .Q(register_1_q));  // open: clr
  Register #(.width(32)) register_2 (.D(rd_value), .en(decoder_1_out2), .clk(in_1), .Q(register_2_q));  // open: clr
  Register #(.width(32)) register_3 (.D(rd_value), .en(decoder_1_out8), .clk(in_1), .Q(register_3_q));  // open: clr
  Register #(.width(32)) register_4 (.D(rd_value), .en(decoder_1_out9), .clk(in_1), .Q(register_4_q));  // open: clr
  Multiplexer #(.select(5), .width(32)) multiplexer_1 (
    .in0(register_1_q), .in2(register_2_q), .in8(register_3_q), .in9(register_4_q), .in10(register_5_q),
    .in11(register_6_q), .in12(register_7_q), .in13(register_9_q), .in14(register_8_q), .in15(register_10_q),
    .out(rd_value_o), .sel(inst[11:7]));  // open: in1, in3, in4, in5, in6, in7, in16, in17, in18, in19, in20, in21, in22, in23, in24, in25, in26, in27, in28, in29, in30, in31
  Register #(.width(32)) register_5 (.D(rd_value), .en(decoder_1_out10), .clk(in_1), .Q(register_5_q));  // open: clr
  Register #(.width(32)) register_6 (.D(rd_value), .en(decoder_1_out11), .clk(in_1), .Q(register_6_q));  // open: clr
  Register #(.width(32)) register_7 (.D(rd_value), .en(decoder_1_out12), .clk(in_1), .Q(register_7_q));  // open: clr
  Register #(.width(32)) register_8 (.D(rd_value), .en(decoder_1_out14), .clk(in_1), .Q(register_8_q));  // open: clr
  Register #(.width(32)) register_9 (.D(rd_value), .en(decoder_1_out13), .clk(in_1), .Q(register_9_q));  // open: clr
  Register #(.width(32)) register_10 (.D(rd_value), .en(decoder_1_out15), .clk(in_1), .Q(register_10_q));  // open: clr
  Multiplexer #(.select(5), .width(32)) multiplexer_2 (
    .in0(register_1_q), .in2(register_2_q), .in8(register_3_q), .in9(register_4_q), .in10(register_5_q),
    .in11(register_6_q), .in12(register_7_q), .in13(register_9_q), .in14(register_8_q), .in15(register_10_q),
    .out(rs2_value_o), .sel(inst[6:2]));  // open: in1, in3, in4, in5, in6, in7, in16, in17, in18, in19, in20, in21, in22, in23, in24, in25, in26, in27, in28, in29, in30, in31
  Multiplexer #(.select(5), .width(32)) multiplexer_3 (
    .in0(register_1_q), .in2(register_2_q), .in8(register_3_q), .in9(register_4_q), .in10(register_5_q),
    .in11(register_6_q), .in12(register_7_q), .in13(register_9_q), .in14(register_8_q), .in15(register_10_q),
    .out(rs1_short_value_o), .sel({2'b01, inst[9:7]}));  // open: in1, in3, in4, in5, in6, in7, in16, in17, in18, in19, in20, in21, in22, in23, in24, in25, in26, in27, in28, in29, in30, in31

  assign rd_o = inst[11:7];

  // Other names for the same wires on the sheet: clk = in_1; rs2[4:0] = inst[6:2]; rd[4:0] = inst[11:7];
  //   rs1_short[2:0] = inst[9:7]
endmodule

module ALU (
  input  FUNC4,
  input  [31:0] rd_input,
  input  [31:0] rs2_imm_input,
  input  [4:0] select_type,
  input  clk,
  input  rst,
  output [31:0] rd_value_o
);

  wire [4:0] bit_extender_1_out;
  wire [31:0] adder_1_out, multiplexer_1_out, multiplexer_2_out, shifter_1_out, shifter_2_out;

  Bit_Extender #(.in_width(32), .out_width(5)) bit_extender_1 (.in(rs2_imm_input), .out(bit_extender_1_out));
  Adder #(.width(32)) adder_1 (.a(rd_input), .b(rs2_imm_input), .out(adder_1_out));  // open: cin, cout
  Shifter #(.width(32)) shifter_1 (.in(rs2_imm_input), .\dist (5'b01100), .out(shifter_1_out));
  Multiplexer #(.width(32)) multiplexer_1 (
    .in0(rs2_imm_input), .in1(adder_1_out), .out(multiplexer_1_out), .sel(FUNC4));
  Shifter #(.width(32)) shifter_2 (.in(rd_input), .\dist (bit_extender_1_out), .out(shifter_2_out));
  Multiplexer #(.select(5), .width(32)) multiplexer_2 (
    .in8(adder_1_out), .in10(rs2_imm_input), .in11(shifter_1_out), .in16(shifter_2_out),
    .in20(multiplexer_1_out), .out(multiplexer_2_out), .sel(select_type));  // open: in0, in1, in2, in3, in4, in5, in6, in7, in9, in12, in13, in14, in15, in17, in18, in19, in21, in22, in23, in24, in25, in26, in27, in28, in29, in30, in31
  Register #(.width(32)) register_1 (.D(multiplexer_2_out), .clk(clk), .Q(rd_value_o), .clr(rst));  // open: en
endmodule

module PC (
  input  [15:0] instr,
  input  [31:0] current_pc,
  input  FUNC4,
  input  [4:0] select_type,
  input  clk,
  input  rst,
  input  [31:0] rs1,
  input  [31:0] rs1_short_value,
  output [31:0] control_pc,
  output wb_en,
  output control_en
);

  wire if_beqz, rs2_if0;
  wire [31:0] adder_1_out, adder_2_out, adder_3_out, multiplexer_1_out, multiplexer_2_out, multiplexer_3_out;

  Adder #(.width(32)) adder_1 (
    .a(current_pc),
    .b({{20{1'b0}}, instr[12], instr[8], instr[10:9], instr[6], instr[7], instr[2], instr[11], instr[5:3], 1'b0}),
    .out(adder_1_out));  // open: cin, cout
  Adder #(.width(32)) adder_2 (.a(current_pc), .b(32'h1), .out(adder_2_out));  // open: cin, cout
  Multiplexer #(.width(32)) multiplexer_1 (.in1(adder_1_out), .out(multiplexer_1_out), .sel(if_beqz));  // open: in0
  Comparator #(.width(32)) comparator_1 (.a(rs1_short_value), .b({32{1'b0}}), .eq(if_beqz));  // open: gt, lt
  Multiplexer #(.width(32)) multiplexer_2 (.in0(adder_2_out), .in1(rs1), .out(multiplexer_2_out), .sel(rs2_if0));
  Comparator #(.width(5)) comparator_2 (.a(instr[6:2]), .b({5{1'b0}}), .eq(rs2_if0));  // open: gt, lt
  Multiplexer #(.select(5), .width(32)) multiplexer_3 (
    .in0(adder_2_out), .in2(adder_2_out), .in6(adder_2_out), .in8(adder_2_out), .in10(adder_2_out),
    .in11(adder_2_out), .in13(adder_1_out), .in14(multiplexer_1_out), .in16(adder_2_out),
    .in20(multiplexer_2_out), .in22(adder_2_out), .out(multiplexer_3_out));  // open: in1, in3, in4, in5, in7, in9, in12, in15, in17, in18, in19, in21, in23, in24, in25, in26, in27, in28, in29, in30, in31, sel
  Register #(.width(32)) register_1 (.D(multiplexer_3_out), .clk(clk), .Q(control_pc), .clr(rst));  // open: en
  Adder #(.width(32)) adder_3 (.a(current_pc), .b(32'h1), .out(adder_3_out));  // open: cin, cout
  Comparator #(.width(32)) comparator_3 (.a(control_pc), .b(adder_3_out), .eq(wb_en));  // open: gt, lt

  assign control_en = 1'b0;

  // Other names for the same wires on the sheet: offset_beqz[8:1] = {instr[12], instr[6:5], instr[2], instr[11:10], instr[4:3]};
  //   offset_j[11:1] = {instr[12], instr[8], instr[10:9], instr[6], instr[7], instr[2], instr[11], instr[5:3]};
  //   rs2[4:0] = instr[6:2]; rs1_value[31:0] = rs1
endmodule
